// Logisim project Timer_1.circ as structural Verilog: 1 circuit, main circuit main
module main (
  input  f_ext,
  input  PORTB_PB1,
  input  PORTB_PB2,
  output PB1_OC1A,
  output PB2_OC1B,
  output OCF1B,
  output OCF1A,
  output TOV1
);

  wire and_1_out, and_2_out, and_3_out, and_4_out, and_5_out, and_6_out, and_7_out, comparator_1_eq,
       comparator_2_eq, comparator_3_eq, d_ff_1_q, f_clkIO_out, ICR1_set_out, j_k_ff_2_q, j_k_ff_3_q,
       j_k_ff_4_q, j_k_ff_6_q, multiplexer_1_out, not_1_out, not_2_out, not_3_out, not_4_out, OCR1A_set_out,
       OCR1B_set_out, or_1_out, por_1_out, t_ff_1_q, TCCR1A_set_out, TCCR1B_set_out, TCNT1_set_out,
       TIFR1_set_out, TIFR1_val_sw6, TIFR1_val_sw7, TIFR1_val_sw8, TIMSK1_set_out;
  wire [7:0] TCCR1A_q, TCCR1A_val_sw8, TCCR1B_q, TCCR1B_val_sw8, TIMSK1_q, TIMSK1_val_sw8;
  wire [9:0] prescaler_counter_q;
  wire [15:0] ICR1_q, ICR1_val_sw16, OCR1A_q, OCR1A_val_sw16, OCR1B_q, OCR1B_val_sw16, TCNT1_q,
       TCNT1_val_sw16;

  Clock f_clkIO (.out(f_clkIO_out));
  POR por_1 (.out(por_1_out));
  Counter #(.max('h3ff), .width(10)) prescaler_counter (
    .clr(por_1_out), .load(1'b0), .up(1'b1), .count(1'b1), .clk(f_clkIO_out), .D({10{1'b0}}),
    .Q(prescaler_counter_q));  // open: carry
  Button TCCR1B_set (.out(TCCR1B_set_out));
  DipSwitch TCCR1B_val (
    .sw1(TCCR1B_val_sw8[7]), .sw2(TCCR1B_val_sw8[6]), .sw3(TCCR1B_val_sw8[5]), .sw4(TCCR1B_val_sw8[4]),
    .sw5(TCCR1B_val_sw8[3]), .sw6(TCCR1B_val_sw8[2]), .sw7(TCCR1B_val_sw8[1]), .sw8(TCCR1B_val_sw8[0]));
  Register TCCR1B (.D(TCCR1B_val_sw8), .en(TCCR1B_set_out), .clk(f_clkIO_out), .Q(TCCR1B_q), .clr(por_1_out));
  DipSwitch #(.number(16)) TCNT1_val (
    .sw1(TCNT1_val_sw16[15]), .sw2(TCNT1_val_sw16[14]), .sw3(TCNT1_val_sw16[13]), .sw4(TCNT1_val_sw16[12]),
    .sw5(TCNT1_val_sw16[11]), .sw6(TCNT1_val_sw16[10]), .sw7(TCNT1_val_sw16[9]), .sw8(TCNT1_val_sw16[8]),
    .sw9(TCNT1_val_sw16[7]), .sw10(TCNT1_val_sw16[6]), .sw11(TCNT1_val_sw16[5]), .sw12(TCNT1_val_sw16[4]),
    .sw13(TCNT1_val_sw16[3]), .sw14(TCNT1_val_sw16[2]), .sw15(TCNT1_val_sw16[1]), .sw16(TCNT1_val_sw16[0]));
  DipSwitch #(.number(16)) OCR1A_val (
    .sw1(OCR1A_val_sw16[15]), .sw2(OCR1A_val_sw16[14]), .sw3(OCR1A_val_sw16[13]), .sw4(OCR1A_val_sw16[12]),
    .sw5(OCR1A_val_sw16[11]), .sw6(OCR1A_val_sw16[10]), .sw7(OCR1A_val_sw16[9]), .sw8(OCR1A_val_sw16[8]),
    .sw9(OCR1A_val_sw16[7]), .sw10(OCR1A_val_sw16[6]), .sw11(OCR1A_val_sw16[5]), .sw12(OCR1A_val_sw16[4]),
    .sw13(OCR1A_val_sw16[3]), .sw14(OCR1A_val_sw16[2]), .sw15(OCR1A_val_sw16[1]), .sw16(OCR1A_val_sw16[0]));
  DipSwitch #(.number(16)) OCR1B_val (
    .sw1(OCR1B_val_sw16[15]), .sw2(OCR1B_val_sw16[14]), .sw3(OCR1B_val_sw16[13]), .sw4(OCR1B_val_sw16[12]),
    .sw5(OCR1B_val_sw16[11]), .sw6(OCR1B_val_sw16[10]), .sw7(OCR1B_val_sw16[9]), .sw8(OCR1B_val_sw16[8]),
    .sw9(OCR1B_val_sw16[7]), .sw10(OCR1B_val_sw16[6]), .sw11(OCR1B_val_sw16[5]), .sw12(OCR1B_val_sw16[4]),
    .sw13(OCR1B_val_sw16[3]), .sw14(OCR1B_val_sw16[2]), .sw15(OCR1B_val_sw16[1]), .sw16(OCR1B_val_sw16[0]));
  DipSwitch #(.number(16)) ICR1_val (
    .sw1(ICR1_val_sw16[15]), .sw2(ICR1_val_sw16[14]), .sw3(ICR1_val_sw16[13]), .sw4(ICR1_val_sw16[12]),
    .sw5(ICR1_val_sw16[11]), .sw6(ICR1_val_sw16[10]), .sw7(ICR1_val_sw16[9]), .sw8(ICR1_val_sw16[8]),
    .sw9(ICR1_val_sw16[7]), .sw10(ICR1_val_sw16[6]), .sw11(ICR1_val_sw16[5]), .sw12(ICR1_val_sw16[4]),
    .sw13(ICR1_val_sw16[3]), .sw14(ICR1_val_sw16[2]), .sw15(ICR1_val_sw16[1]), .sw16(ICR1_val_sw16[0]));
  not not_1 (not_1_out, f_ext);
  Multiplexer #(.select(3)) multiplexer_1 (
    .in0(1'b0), .in1(f_clkIO_out), .in2(prescaler_counter_q[2]), .in3(prescaler_counter_q[5]),
    .in4(prescaler_counter_q[7]), .in5(prescaler_counter_q[9]), .in6(not_1_out), .in7(f_ext),
    .out(multiplexer_1_out), .sel(TCCR1B_q[2:0]));
  Button TCNT1_set (.out(TCNT1_set_out));
  Button OCR1A_set (.out(OCR1A_set_out));
  Button OCR1B_set (.out(OCR1B_set_out));
  Button ICR1_set (.out(ICR1_set_out));
  Counter #(.max('hffff), .width(16)) TCNT1 (
    .clr(or_1_out), .load(TCNT1_set_out), .up(1'b1), .count(1'b1), .clk(multiplexer_1_out),
    .D(TCNT1_val_sw16), .Q(TCNT1_q));  // open: carry
  Register #(.width(16)) OCR1A (
    .D(OCR1A_val_sw16), .en(OCR1A_set_out), .clk(f_clkIO_out), .Q(OCR1A_q), .clr(por_1_out));
  Register #(.width(16)) OCR1B (
    .D(OCR1B_val_sw16), .en(OCR1B_set_out), .clk(f_clkIO_out), .Q(OCR1B_q), .clr(por_1_out));
  Register #(.width(16)) ICR1 (.D(ICR1_val_sw16), .en(ICR1_set_out), .clk(f_clkIO_out), .Q(ICR1_q), .clr(por_1_out));
  DipSwitch TIMSK1_val (
    .sw1(TIMSK1_val_sw8[7]), .sw2(TIMSK1_val_sw8[6]), .sw3(TIMSK1_val_sw8[5]), .sw4(TIMSK1_val_sw8[4]),
    .sw5(TIMSK1_val_sw8[3]), .sw6(TIMSK1_val_sw8[2]), .sw7(TIMSK1_val_sw8[1]), .sw8(TIMSK1_val_sw8[0]));
  Button TIMSK1_set (.out(TIMSK1_set_out));
  not not_2 (not_2_out, f_clkIO_out);
  Register TIMSK1 (.D(TIMSK1_val_sw8), .en(TIMSK1_set_out), .clk(f_clkIO_out), .Q(TIMSK1_q), .clr(por_1_out));
  D_Flip_Flop d_ff_1 (.D(comparator_3_eq), .clk(not_2_out), .Q(d_ff_1_q), .reset(por_1_out));  // open: Qn, preset
  Comparator #(.mode("unsigned"), .width(16)) comparator_1 (
    .a(TCNT1_q), .b(OCR1A_q), .eq(comparator_1_eq));  // open: gt, lt
  Comparator #(.mode("unsigned"), .width(16)) comparator_2 (
    .a(TCNT1_q), .b(OCR1B_q), .eq(comparator_2_eq));  // open: gt, lt
  Comparator #(.mode("unsigned"), .width(16)) comparator_3 (
    .a(TCNT1_q), .b(ICR1_q), .eq(comparator_3_eq));  // open: gt, lt
  and and_1 (and_1_out, comparator_1_eq, TIMSK1_q[1]);
  not not_3 (not_3_out, f_clkIO_out);
  T_Flip_Flop t_ff_1 (
    .T(comparator_1_eq), .clk(not_3_out), .Q(t_ff_1_q), .reset(por_1_out), .preset(1'b0));  // open: Qn
  and and_2 (and_2_out, comparator_2_eq, TIMSK1_q[2]);
  and and_3 (and_3_out, comparator_3_eq, TIMSK1_q[0]);
  not not_4 (not_4_out, f_clkIO_out);
  and and_4 (and_4_out, TIFR1_set_out, TIFR1_val_sw6);
  Button TIFR1_set (.out(TIFR1_set_out));
  and and_5 (and_5_out, f_clkIO_out, d_ff_1_q);
  J_K_Flip_Flop j_k_ff_1 (
    .J(and_2_out), .K(and_4_out), .clk(not_4_out), .Q(OCF1B), .preset(1'b0), .reset(por_1_out));  // open: Qn
  DipSwitch TIFR1_val (.sw6(TIFR1_val_sw6), .sw7(TIFR1_val_sw7), .sw8(TIFR1_val_sw8));  // open: sw1, sw2, sw3, sw4, sw5
  or or_1 (or_1_out, and_5_out, por_1_out);
  J_K_Flip_Flop j_k_ff_2 (
    .J(comparator_3_eq), .K(comparator_1_eq), .clk(not_3_out), .Q(j_k_ff_2_q), .preset(1'b0),
    .reset(por_1_out));  // open: Qn
  Button TCCR1A_set (.out(TCCR1A_set_out));
  DipSwitch TCCR1A_val (
    .sw1(TCCR1A_val_sw8[7]), .sw2(TCCR1A_val_sw8[6]), .sw3(TCCR1A_val_sw8[5]), .sw4(TCCR1A_val_sw8[4]),
    .sw5(TCCR1A_val_sw8[3]), .sw6(TCCR1A_val_sw8[2]), .sw7(TCCR1A_val_sw8[1]), .sw8(TCCR1A_val_sw8[0]));
  J_K_Flip_Flop j_k_ff_3 (
    .J(comparator_3_eq), .K(comparator_2_eq), .clk(not_3_out), .Q(j_k_ff_3_q), .preset(1'b0),
    .reset(por_1_out));  // open: Qn
  and and_6 (and_6_out, TIFR1_set_out, TIFR1_val_sw7);
  J_K_Flip_Flop j_k_ff_4 (
    .J(comparator_1_eq), .K(comparator_3_eq), .clk(not_3_out), .Q(j_k_ff_4_q), .preset(1'b0),
    .reset(por_1_out));  // open: Qn
  Register TCCR1A (.D(TCCR1A_val_sw8), .en(TCCR1A_set_out), .clk(f_clkIO_out), .Q(TCCR1A_q), .clr(por_1_out));
  J_K_Flip_Flop j_k_ff_5 (
    .J(and_1_out), .K(and_6_out), .clk(not_4_out), .Q(OCF1A), .preset(1'b0), .reset(por_1_out));  // open: Qn
  J_K_Flip_Flop j_k_ff_6 (
    .J(comparator_2_eq), .K(comparator_3_eq), .clk(not_3_out), .Q(j_k_ff_6_q), .preset(1'b0),
    .reset(por_1_out));  // open: Qn
  and and_7 (and_7_out, TIFR1_set_out, TIFR1_val_sw8);
  Multiplexer #(.select(2)) multiplexer_2 (
    .in0(PORTB_PB1), .in1(t_ff_1_q), .in2(j_k_ff_2_q), .in3(j_k_ff_4_q), .out(PB1_OC1A), .sel(TCCR1A_q[7:6]));
  Multiplexer #(.select(2)) multiplexer_3 (
    .in0(PORTB_PB2), .in1(PORTB_PB2), .in2(j_k_ff_3_q), .in3(j_k_ff_6_q), .out(PB2_OC1B), .sel(TCCR1A_q[5:4]));
  J_K_Flip_Flop j_k_ff_7 (
    .J(and_3_out), .K(and_7_out), .clk(not_4_out), .Q(TOV1), .preset(1'b0), .reset(por_1_out));  // open: Qn

  // Notes on the sheet:
  //   CSx
  //   TOP
  //   TIFR1
  //   COM1A1
  //   COM1B0
  //   COM1A0
  //   COM1B1
endmodule
